# Fritzing sketch hestia-B+ (saved by Fritzing 0.9.1b)
circuit board: 5.59679cm x 5.19671cm
breadboards: 1

parts:
  R5 = Trimmer Potentiometer [maximum_resistance=10kΩ package=THT]
  R2-1 = Resistor [tolerance=±5% resistance=1k package="1206 [SMD]"]
  R1-1 = Resistor [tolerance=±5% resistance=10k package="1206 [SMD]"]
  R2-2 = Resistor [tolerance=±5% resistance=1k package="1206 [SMD]"]
  R1-2 = Resistor [tolerance=±5% resistance=10k package="1206 [SMD]"]
  R1-3 = Resistor [tolerance=±5% resistance=10k package="1206 [SMD]"]
  R2-3 = Resistor [tolerance=±5% resistance=1k package="1206 [SMD]"]
  R1-4 = Resistor [tolerance=±5% resistance=10k package="1206 [SMD]"]
  R2-4 = Resistor [tolerance=±5% resistance=1k package="1206 [SMD]"]
  LCD = LCD screen
  S1_(H) = Pushbutton [package="[THT]"]
  S2_(-) = Pushbutton [package="[THT]"]
  S3_(+) = Pushbutton [package="[THT]"]
  S4_(W) = Pushbutton [package="[THT]"]
  RESET = Pushbutton [package="[THT]"]
  RESET_2 = female pin header, 2 pins [form="♀ (female)"]
  C1 = Capacitor [part_number=100nF package=0805]
  R4 = Resistor [tolerance=±5% resistance=27k package="1206 [SMD]"]
  Q1 = NPN-Transistor [package="SOT-23 [SMD]"]
  R3 = Resistor [tolerance=±5% resistance=4.7k package="1206 [SMD]"]
  Pi = Adafruit Pi Cobbler
  W = LEDs [package=led-1206]
  H = LEDs [package=led-1206]
  R5_2 = Resistor [tolerance=±5% resistance=130 package="1206 [SMD]"]
  R6 = Resistor [tolerance=±5% resistance=130 package="1206 [SMD]"]
  RELAY = female pin header, 4 pins [form="♀ (female)"]
  18B20 = NPN-Transistor [package="TO92 [THT]"]

nets:
  VSS: R5.leg1, LCD.VSS, LCD.R/W, LCD.DB0, LCD.DB1, LCD.DB2, LCD.DB3, S1_(H).Pin_3, S1_(H).Pin_4, S2_(-).Pin_3, S2_(-).Pin_4, S3_(+).Pin_3, S3_(+).Pin_4, S4_(W).Pin_3, S4_(W).Pin_4, C1.2, Q1.2, Pi.GND, RELAY.pin1, 18B20.E
  N1: R5.wiper, LCD.V0
  N2: R5.leg2, LCD.VDD, LCD.LED+, C1.1, Pi.5V0, R5_2.Pin_0, R6.Pin_0, RELAY.pin4
  N3: R2-1.Pin_0, R1-1.Pin_0, S1_(H).Pin_1, S1_(H).Pin_2
  N4: R2-1.Pin_1, Pi.#24
  N5: R1-1.Pin_1, R1-2.Pin_0, R1-3.Pin_0, R1-4.Pin_0, R3.Pin_0, Pi.3V3, 18B20.B
  N6: R2-2.Pin_0, R1-2.Pin_1, S2_(-).Pin_1, S2_(-).Pin_2
  N7: R2-2.Pin_1, Pi.#17
  N8: R1-3.Pin_1, R2-3.Pin_0, S3_(+).Pin_1, S3_(+).Pin_2
  N9: R2-3.Pin_1, Pi.#22
  N10: R1-4.Pin_1, R2-4.Pin_0, S4_(W).Pin_1, S4_(W).Pin_2
  N11: R2-4.Pin_1, Pi.CE1
  N12: LCD.RS, Pi.CE0
  N13: LCD.E, Pi.#25
  N14: LCD.DB4, Pi.MOSI
  N15: LCD.DB5, Pi.RXD
  N16: LCD.DB6, Pi.SCLK
  N17: LCD.DB7, Pi.TXD
  N18: LCD.LED-, Q1.1
  N19: RESET.Pin_1, RESET.Pin_2, RESET_2.pin2
  N20: RESET.Pin_3, RESET.Pin_4, RESET_2.pin1
  N21: R4.Pin_0, Q1.0
  N22: R4.Pin_1, Pi.MISO
  N23: R3.Pin_1, Pi.#4, 18B20.C
  N24: Pi.#18, H.C, RELAY.pin2
  N25: Pi.#23, W.C, RELAY.pin3
  N26: W.A, R6.Pin_1
  N27: H.A, R5_2.Pin_1

notes:
  HestiaPi v0.5

custom parts:
  Adafruit Pi Cobbler: Adafruit Pi Cobbler GPIO Breakout for Raspberry Pi
