# Fritzing sketch hestia (saved by Fritzing 0.8.5b)
circuit board: 3.69604cm x 3.60099cm
breadboards: 1

parts:
  Pi1 = Adafruit Pi Cobbler
  RL_RL1 = female pin header, 1 pin [form="♀ (female)"]
  RL_GND = female pin header, 1 pin [form="♀ (female)"]
  RL_RL2 = female pin header, 1 pin [form="♀ (female)"]
  LCD_GND = female pin header, 1 pin [form="♀ (female)"]
  LCD_V0 = female pin header, 1 pin [form="♀ (female)"]
  LCD_RS = female pin header, 1 pin [form="♀ (female)"]
  LCD_E = female pin header, 1 pin [form="♀ (female)"]
  LCD_LED- = female pin header, 1 pin [form="♀ (female)"]
  LCD_DB4 = female pin header, 1 pin [form="♀ (female)"]
  LCD_DB5 = female pin header, 1 pin [form="♀ (female)"]
  LCD_DB6 = female pin header, 1 pin [form="♀ (female)"]
  LCD_DB7 = female pin header, 1 pin [form="♀ (female)"]
  R5 = Trimmer Potentiometer [maximum_resistance=10kΩ package=THT]
  18B20 = female pin header, 3 pins [form="♀ (female)"]
  RL_Vcc = female pin header, 1 pin [form="♀ (female)"]
  LCD_VDD = female pin header, 1 pin [form="♀ (female)"]
  R4 = Resistor [tolerance=±5% resistance=27k package="1206 [SMD]"]
  Q1 = NPN-Transistor [package="SOT-23 [SMD]"]
  R3 = Resistor [tolerance=±5% resistance=4.7k package="1206 [SMD]"]
  R2 = Resistor [tolerance=±5% resistance=1k package="1206 [SMD]"]
  R1 = Resistor [tolerance=±5% resistance=10k package="1206 [SMD]"]
  R2_2 = Resistor [tolerance=±5% resistance=1k package="1206 [SMD]"]
  R1_2 = Resistor [tolerance=±5% resistance=10k package="1206 [SMD]"]
  R1_3 = Resistor [tolerance=±5% resistance=10k package="1206 [SMD]"]
  R2_3 = Resistor [tolerance=±5% resistance=1k package="1206 [SMD]"]
  R1_4 = Resistor [tolerance=±5% resistance=10k package="1206 [SMD]"]
  R2_4 = Resistor [tolerance=±5% resistance=1k package="1206 [SMD]"]
  LED1 = LEDs [package=led-0603]  # not connected
  LED2 = LEDs [package=led-0603]  # not connected
  S2 = Pushbutton [package="[THT]"]
  S1 = Pushbutton [package="[THT]"]
  S4 = Pushbutton [package="[THT]"]
  S3 = Pushbutton [package="[THT]"]

nets:
  N1: Pi1.3V3, 18B20.pin1, R3.Pin_0, R1.Pin_1, R1_2.Pin_0, R1_3.Pin_0, R1_4.Pin_0
  N2: Pi1.5V0, R5.leg2, RL_Vcc.pin1, LCD_VDD.pin1
  N3: Pi1.GND, RL_GND.pin1, LCD_GND.pin1, R5.leg1, 18B20.pin3, Q1.2, S2.Pin_3, S2.Pin_4, S1.Pin_3, S1.Pin_4, S4.Pin_3, S4.Pin_4, S3.Pin_3, S3.Pin_4
  N4: Pi1.#4, 18B20.pin2, R3.Pin_1
  N5: Pi1.TXD, LCD_DB7.pin1
  N6: Pi1.RXD, LCD_DB5.pin1
  N7: Pi1.#17, R2_2.Pin_1
  N8: Pi1.#18, RL_RL1.pin1
  N9: Pi1.#22, R2_3.Pin_1
  N10: Pi1.#23, RL_RL2.pin1
  N11: Pi1.#24, R2.Pin_1
  N12: Pi1.MOSI, LCD_DB4.pin1
  N13: Pi1.MISO, R4.Pin_1
  N14: Pi1.#25, LCD_E.pin1
  N15: Pi1.SCLK, LCD_DB6.pin1
  N16: Pi1.CE0, LCD_RS.pin1
  N17: Pi1.CE1, R2_4.Pin_1
  N18: LCD_V0.pin1, R5.wiper
  N19: LCD_LED-.pin1, Q1.1
  N20: R4.Pin_0, Q1.0
  N21: R2.Pin_0, R1.Pin_0, S1.Pin_1, S1.Pin_2
  N22: R2_2.Pin_0, R1_2.Pin_1, S4.Pin_1, S4.Pin_2
  N23: R1_3.Pin_1, R2_3.Pin_0, S3.Pin_1, S3.Pin_2
  N24: R1_4.Pin_1, R2_4.Pin_0, S2.Pin_1, S2.Pin_2

notes:
  HestiaPi v0.4

custom parts:
  Adafruit Pi Cobbler: Adafruit Pi Cobbler GPIO Breakout for Raspberry Pi
