# Fritzing sketch v1-no-socket (saved by Fritzing 0.8.3b)
circuit board: 4.36491cm x 5.58677cm
breadboards: 1

parts:
  S1 = Pushbutton [part_number=S1 package="[THT]"]
  S2 = Pushbutton [part_number=S2 package="[THT]"]
  R2 = Resistor [tolerance=±5% resistance=1k package="1206 [SMD]"]
  R1 = Resistor [tolerance=±5% resistance=10k package="1206 [SMD]"]
  R1_2 = Resistor [tolerance=±5% resistance=10k package="1206 [SMD]"]
  R2_2 = Resistor [tolerance=±5% resistance=1k package="1206 [SMD]"]
  R4 = Resistor [tolerance=±5% resistance=27k package="1206 [SMD]"]
  Q2 = NPN-Transistor [package="TO92 [THT]"]
  S3 = Pushbutton [part_number=S3 package="[THT]"]
  S4 = Pushbutton [part_number=S4 package="[THT]"]
  R1_3 = Resistor [tolerance=±5% resistance=10k package="1206 [SMD]"]
  R1_4 = Resistor [tolerance=±5% resistance=10k package="1206 [SMD]"]
  R2_3 = Resistor [tolerance=±5% resistance=1k package="1206 [SMD]"]
  R2_4 = Resistor [tolerance=±5% resistance=1k package="1206 [SMD]"]
  Q1 = NPN-Transistor [package="SOT-23 [SMD]"]
  R3 = Resistor [tolerance=±5% resistance=4.7k package="1206 [SMD]"]
  Pi1 = Adafruit Pi Cobbler
  RL_RL1 = female pin header, 1 pin [form="♀ (female)"]
  RL_GND = female pin header, 1 pin [form="♀ (female)"]
  RL_Vcc = female pin header, 1 pin [form="♀ (female)"]
  RL_RL2 = female pin header, 1 pin [form="♀ (female)"]
  LCD_GND = female pin header, 1 pin [form="♀ (female)"]
  LCD_VDD = female pin header, 1 pin [form="♀ (female)"]
  LCD_V0 = female pin header, 1 pin [form="♀ (female)"]
  LCD_RS = female pin header, 1 pin [form="♀ (female)"]
  LCD_E = female pin header, 1 pin [form="♀ (female)"]
  LCD_LED- = female pin header, 1 pin [form="♀ (female)"]
  LCD_DB4 = female pin header, 1 pin [form="♀ (female)"]
  LCD_DB5 = female pin header, 1 pin [form="♀ (female)"]
  LCD_DB6 = female pin header, 1 pin [form="♀ (female)"]
  LCD_DB7 = female pin header, 1 pin [form="♀ (female)"]
  R5 = Trimmer Potentiometer [maximum_resistance=10kΩ package=THT]

nets:
  N1: S1.Pin_1, S1.Pin_2, R2.Pin_0, R1.Pin_1
  N2: S1.Pin_3, S1.Pin_4, S2.Pin_3, S2.Pin_4, Q2.E, S3.Pin_3, S3.Pin_4, S4.Pin_3, S4.Pin_4, Q1.2, Pi1.GND, RL_GND.pin1, LCD_GND.pin1, R5.leg1
  N3: S2.Pin_1, S2.Pin_2, R1_2.Pin_0, R2_2.Pin_0
  N4: R2.Pin_1, Pi1.#17
  N5: R1.Pin_0, R1_2.Pin_1, Q2.C, R1_3.Pin_0, R1_4.Pin_0, R3.Pin_0, Pi1.3V3
  N6: R2_2.Pin_1, Pi1.#24
  N7: R4.Pin_0, Q1.0
  N8: R4.Pin_1, Pi1.MISO
  N9: Q2.B, R3.Pin_1, Pi1.#4
  N10: S3.Pin_1, S3.Pin_2, R1_4.Pin_1, R2_4.Pin_0
  N11: S4.Pin_1, S4.Pin_2, R1_3.Pin_1, R2_3.Pin_0
  N12: R2_3.Pin_1, Pi1.CE1
  N13: R2_4.Pin_1, Pi1.#22
  N14: Q1.1, LCD_LED-.pin1
  N15: Pi1.5V0, RL_Vcc.pin1, LCD_VDD.pin1, R5.leg2
  N16: Pi1.TXD, LCD_DB7.pin1
  N17: Pi1.RXD, LCD_DB5.pin1
  N18: Pi1.#18, RL_RL1.pin1
  N19: Pi1.#23, RL_RL2.pin1
  N20: Pi1.MOSI, LCD_DB4.pin1
  N21: Pi1.#25, LCD_E.pin1
  N22: Pi1.SCLK, LCD_DB6.pin1
  N23: Pi1.CE0, LCD_RS.pin1
  N24: LCD_V0.pin1, R5.wiper

notes:
  Hestia v0.3

custom parts:
  Adafruit Pi Cobbler: Adafruit Pi Cobbler GPIO Breakout for Raspberry Pi
