# Fritzing sketch v1-no-socket (saved by Fritzing 0.7.12b)
breadboards: 1

parts:
  S1 = Pushbutton [part_number=S1 package="[THT]"]
  S2 = Pushbutton [part_number=S2 package="[THT]"]
  R2 = Resistor [tolerance=±5% resistance=1k package="1206 [SMD]"]
  R1 = Resistor [tolerance=±5% resistance=10k package="1206 [SMD]"]
  R3 = Resistor [tolerance=±5% resistance=10k package="1206 [SMD]"]
  R4 = Resistor [tolerance=±5% resistance=1k package="1206 [SMD]"]
  R10 = Resistor [tolerance=±5% resistance=27k package="1206 [SMD]"]
  R9 = Trimmer Potentiometer [maximum_resistance=10kΩ package=THT]
  Q2 = NPN-Transistor [package="TO92 [THT]"]
  S3 = Pushbutton [package="[THT]"]
  S4 = Pushbutton [package="[THT]"]
  R7 = Resistor [tolerance=±5% resistance=10k package="1206 [SMD]"]
  R5 = Resistor [tolerance=±5% resistance=10k package="1206 [SMD]"]
  R8 = Resistor [tolerance=±5% resistance=1k package="1206 [SMD]"]
  R6 = Resistor [tolerance=±5% resistance=1k package="1206 [SMD]"]
  Q1 = NPN-Transistor [package="SOT-23 [SMD]"]
  R11 = Resistor [tolerance=±5% resistance=4.7k package="1206 [SMD]"]
  RL1 = 2-Channel Relay Module [part_number=RL1]
  Pi1 = Adafruit Pi Cobbler
  LCD1 = LCD screen

nets:
  N1: S1.Pin_1, S1.Pin_2, R2.Pin_0, R1.Pin_1
  GND: S1.Pin_3, S1.Pin_4, S2.Pin_3, S2.Pin_4, R9.leg1, Q2.E, S3.Pin_3, S3.Pin_4, S4.Pin_3, S4.Pin_4, Q1.2, RL1.GND, Pi1.GND, Pi1.PIN9, Pi1.PIN14, Pi1.PIN20, Pi1.PIN25, LCD1.VSS, LCD1.R/W, LCD1.DB0, LCD1.DB1, LCD1.DB2, LCD1.DB3
  N2: S2.Pin_1, S2.Pin_2, R3.Pin_0, R4.Pin_0
  N3: R2.Pin_1, Pi1.#17
  N4: R1.Pin_0, R3.Pin_1, R7.Pin_0, R5.Pin_0, Pi1.3V3
  N5: R4.Pin_1, Pi1.#24
  N6: R10.Pin_0, Q1.0
  N7: R10.Pin_1, Pi1.MISO
  N8: R9.wiper, LCD1.V0
  VCC: R9.leg2, RL1.Vcc, Pi1.5V0, LCD1.VDD, LCD1.LED+
  N9: Q2.B, R11.Pin_1, Pi1.#4
  N10: Q2.C, R11.Pin_0
  N11: S3.Pin_1, S3.Pin_2, R5.Pin_1, R6.Pin_0
  N12: S4.Pin_1, S4.Pin_2, R7.Pin_1, R8.Pin_0
  N13: R8.Pin_1, Pi1.CE1
  N14: R6.Pin_1, Pi1.#22
  N15: Q1.1, LCD1.LED-
  N16: RL1.IN1, Pi1.TXD
  N17: RL1.IN2, Pi1.RXD
  N18: Pi1.#18, LCD1.DB7
  N19: Pi1.#21, LCD1.DB6
  N20: Pi1.#23, LCD1.DB5
  N21: Pi1.MOSI, LCD1.DB4
  N22: Pi1.#25, LCD1.E
  N23: Pi1.CE0, LCD1.RS

notes:
  Hestia v1.0

custom parts:
  2-Channel Relay Module: 2-Channel Relay Module Board Shield With optocoupler
  Adafruit Pi Cobbler: Adafruit Pi Cobbler GPIO Breakout for Raspberry Pi
